# Fritzing sketch Smart Alarm (saved by Fritzing 1.0.4)
breadboards: 1

parts:
  J1 = STM32 Nucleo boards
  OLED_I2C1 = OLED 128x64 I2C Monochrome Display
  A1 = Wemos S2 Mini [part_number="WeMos D1 Mini Lite"]
  Keypad4x2 = Keypad Membran 4x4
  Reed_Switch = SWITCH-MOMENTARY-2 [package=reed_switch_pth]
  J2 = Piezo Speaker
  10K = Resistor [tolerance=±5% power=0.25W resistance=220 package=THT]
  PIR1 = PIR sensor
  10K_2 = Resistor [tolerance=±5% power=0.25W resistance=220 package=THT]
  10K_3 = Resistor [tolerance=±5% power=0.25W resistance=220 package=THT]
  ResetPin = PN532 Elechouse RFID NFC Module V3

nets:
  N1: J1.PC6, Keypad4x2.Pin5
  N2: J1.PC5, Keypad4x2.Pin8
  N3: J1.PB12, ResetPin.A10
  N4: J1.D2, J2.pin2
  N5: J1.D4, A1.Pin_1, A1.Pin_9
  N6: J1.D7, Reed_Switch.2, 10K.Pin_1
  5V: J1.5V, A1.Pin_17, A1.Pin_25, PIR1.VDD, ResetPin.VCC
  N7: J1.PB2, Keypad4x2.Pin3
  N8: J1.PB1, Keypad4x2.Pin2
  N9: J1.PB15, Keypad4x2.Pin1
  N10: J1.PC4, Keypad4x2.Pin7
  N11: J1.PB8, A1.Pin_24, A1.Pin_32, 10K_2.Pin_0, ResetPin.SCL
  N12: J1.PB9, OLED_I2C1.SDA, A1.Pin_23, A1.Pin_31, 10K_3.Pin_0
  N13: J1.PC7, Keypad4x2.Pin6
  N14: J1.PB10, Keypad4x2.Pin4
  GND: J1.GND, OLED_I2C1.GND, A1.Pin_18, A1.Pin_26, Reed_Switch.1, J2.pin1, PIR1.GND, ResetPin.GND
  N15: J1.PB7, PIR1.SIG
  N16: OLED_I2C1.VDD, 10K.Pin_0, 10K_2.Pin_1, 10K_3.Pin_1
  N17: A1.Pin_2, A1.Pin_10
  N18: A1.Pin_3, A1.Pin_11
  N19: A1.Pin_4, A1.Pin_12
  N20: A1.Pin_5, A1.Pin_13
  N21: A1.Pin_6, A1.Pin_14
  N22: A1.Pin_7, A1.Pin_15
  N23: A1.Pin_8, A1.Pin_16
  N24: A1.Pin_19, A1.Pin_27
  N25: A1.Pin_20, A1.Pin_28
  N26: A1.Pin_21, A1.Pin_29
  N27: A1.Pin_22, A1.Pin_30

custom parts:
  Wemos S2 Mini: A mini wifi board based on the ESP32-S2FN4R2.
  Keypad Membran 4x4: Membrane Keypad 4x4 Matrix
  PN532 Elechouse RFID NFC Module V3: NFC is a popular technology in recent years. We often heard this work while smart phone company such as Samsung or HTC introduces their latest high-end phones. Almost all the high-end phone in the market support NFC. Near field communication (NFC) is a set of standards for smart phones and similar devices to establish radio communication with each other by touching them together or bringing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
